# Fritzing sketch CIRCUIT HAND (saved by Fritzing 0.9.3b)

parts:
  M1 = MAX30102
  Part1 = NRF24L01+ Breakout Board
  Part2 = ESP-WROOM-32 [ESP-32S] Module [part_number=ESP-WROOM-32]

nets:
  VIN: M1.VIN, Part1.VCC, Part2.3V3
  N1: M1.SCL, Part2.IO25
  N2: M1.SDA, Part2.IO4
  N3: M1.GND, Part2.GND#0
  N4: Part1.GND, Part2.GND#51
  N5: Part1.CE, Part2.IO16
  N6: Part1.CS, Part2.IO12
  N7: Part1.SCK, Part2.IO18
  N8: Part1.MOSI, Part2.IO23
  N9: Part1.MISO, Part2.IO19

custom parts:
  MAX30102: Oximeter module using the MAX30102 chip. You may wish to read (and check your module) this post on power problems with these modules: https://reedpaper.wordpress.com/2018/08/22/pulse-oximeter-max30100-max30102-how-to-fix-wrong-board/ . As usual, if you want the mounting holes in pcb, you need to drag a hole over the pad in silkscreen to actually drill the hole (by default they are not drilled)
  ESP-WROOM-32 [ESP-32S] Module: Espressif ESP-WROOM-32 WiFi/Bluetooth LE microcontroller module also known as the Ai-Thinker ESP-32S module with similar formfactor. The ESP32 is a microcontroller chip with WiFi and BLE capabilities. The chip is developed by Espressif and is the successor to the popular ESP8266 WiFi module.
